// Logisim project 4BITCPU4YOUTUBERS.circ as structural Verilog: 2 circuits, main circuit main
module main (
  input  SUB,
  input  CIN,
  input  [2:0] in_3,
  input  A,
  input  B,
  input  LESS,
  output out_7,
  output COUT,
  output SET
);

  wire and_1_out, nor_1_out, or_1_out, xor_1_out, xor_2_out;

  xor xor_1 (xor_1_out, B, SUB);
  and and_1 (and_1_out, A, B);
  or or_1 (or_1_out, A, B);
  xor xor_2 (xor_2_out, A, B);
  nor nor_1 (nor_1_out, A, B);
  Adder #(.width(1)) adder_1 (.a(A), .b(xor_1_out), .out(SET), .cin(CIN), .cout(COUT));
  Multiplexer #(.select(3)) multiplexer_1 (
    .in0(and_1_out), .in1(or_1_out), .in2(xor_2_out), .in3(nor_1_out), .in4(SET), .in5(LESS), .out(out_7),
    .sel(in_3));  // open: in6, in7, en
endmodule

module _4BITALUCPU (
  input  SUB,
  input  [2:0] in_2,
  input  [3:0] A,
  input  [3:0] B,
  output [3:0] RESULT,
  output ZERO_FLAG
);

  wire main_1_cout, main_2_cout, main_3_cout, main_4_set;

  main main_1 (
    .A(A[0]), .B(B[0]), .out_7(RESULT[0]), .SUB(SUB), .CIN(SUB), .in_3(in_2), .COUT(main_1_cout),
    .LESS(main_4_set));  // open: SET
  main main_2 (
    .A(A[1]), .B(B[1]), .out_7(RESULT[1]), .SUB(SUB), .CIN(main_1_cout), .in_3(in_2), .COUT(main_2_cout),
    .LESS(1'b0));  // open: SET
  main main_3 (
    .A(A[2]), .B(B[2]), .out_7(RESULT[2]), .SUB(SUB), .CIN(main_2_cout), .in_3(in_2), .COUT(main_3_cout),
    .LESS(1'b0));  // open: SET
  main main_4 (
    .A(A[3]), .B(B[3]), .out_7(RESULT[3]), .SUB(SUB), .CIN(main_3_cout), .in_3(in_2), .LESS(1'b0),
    .SET(main_4_set));  // open: COUT
  nor nor_1 (ZERO_FLAG, RESULT[0], RESULT[1], RESULT[2], RESULT[3]);

  // Notes on the sheet:
  //   FUNCTION SELECTOR
endmodule
